// Logisim project Register File.circ as structural Verilog: 1 circuit, main circuit Register File
module Register_File (
  input  [7:0] dbus,
  input  [7:0] dval,
  input  [7:0] sbus,
  output zero,
  output Negative
);

  wire demultiplexer_1_out0, demultiplexer_1_out1, demultiplexer_1_out2, demultiplexer_1_out3, or_1_out,
       undriven, undriven_3;
  wire [1:0] undriven_2, undriven_4, undriven_5;
  wire [7:0] register_1_q, register_2_q, register_3_q, register_4_q;

  Demultiplexer #(.select(2)) demultiplexer_1 (
    .out0(demultiplexer_1_out0), .out1(demultiplexer_1_out1), .out2(demultiplexer_1_out2),
    .out3(demultiplexer_1_out3), .in(undriven), .sel(undriven_2));  // open: en
  Register register_1 (.D(dval), .en(demultiplexer_1_out0), .Q(register_1_q), .clk(undriven_3));  // open: clr
  Register register_2 (.D(dval), .en(demultiplexer_1_out1), .Q(register_2_q), .clk(undriven_3));  // open: clr
  Register register_3 (.D(dval), .en(demultiplexer_1_out2), .Q(register_3_q), .clk(undriven_3));  // open: clr
  Register register_4 (.D(dval), .en(demultiplexer_1_out3), .Q(register_4_q), .clk(undriven_3));  // open: clr
  Multiplexer #(.select(2), .width(8)) multiplexer_1 (
    .in0(register_1_q), .in1(register_2_q), .in2(register_3_q), .in3(register_4_q), .out(dbus),
    .sel(undriven_4));  // open: en
  Multiplexer #(.select(2), .width(8)) multiplexer_2 (
    .in0(register_1_q), .in1(register_2_q), .in2(register_3_q), .in3(register_4_q), .out(sbus),
    .sel(undriven_5));  // open: en
  not not_1 (zero, or_1_out);
  or or_1 (or_1_out, dbus[0], dbus[1], dbus[2], dbus[3], dbus[4], dbus[5], dbus[6], dbus[7]);

  assign Negative = dbus[7];

  // Notes on the sheet:
  //   dwrite
  //   drs
  //   Clock
  //   drs
  //   dregsel
  //   sregsel
endmodule
