// Logisim project CPU-2014-Proj.circ as structural Verilog: 7 circuits, main circuit main
module main (
  input  Writing_Phase_1,
  input  Writing_Phase_2,
  input  Reset_Phase_2,
  input  Reset,
  output [7:0] address,
  output [7:0] r0,
  output [1:0] out_7,
  output [7:0] r1,
  output [7:0] r2,
  output [7:0] r3,
  output [7:0] datain,
  output [7:0] dbus,
  output [7:0] aluout,
  output [7:0] sbus,
  output [7:0] dval,
  output [3:0] out_16,
  output [1:0] aluop,
  output [4:0] out_18,
  output [1:0] phase,
  output pcload,
  output pcsel
);

  wire and_3_p2, and_4_out, and_5_out, and_6_out, c, clock, dwrite, imload, irload, not_1_out, not_2_out,
       not_3_out, not_4_out, not_5_out, or_1_out, or_2_out, or_3_out, or_5_out, or_6_out, or_7_out, or_8_out,
       or_9_out, or_10_out, readwrite, register_2_negative, register_2_zero, two;
  wire [1:0] counter_2_q, dregsel, regsel, sregsel;
  wire [2:0] counter_3_q;
  wire [3:0] ram_1_data;
  wire [3:3] and_2_out;
  wire [6:0] keyboard_1_data;
  wire [7:0] addinstructions_1_output, counter_1_q, counter_4_q, Immediate_q, Instruction_Register_q,
       multiplexer_2_out, multiplexer_3_out, multiplexer_6_out, pc_adder_1_pc_out, register_1_q;

  not not_1 (not_1_out, Reset);
  Keyboard_part #(.buflen(64)) keyboard_1 (
    .clk(clock), .re(Writing_Phase_1), .clr(Reset), .data(keyboard_1_data));  // open: avail
  and and_1 (clock, not_1_out, c);
  and and_2 (and_2_out[3], keyboard_1_data[5], keyboard_1_data[6], 1'b1);
  Adder #(.width(5)) adder_1 (
    .a({2'b00, keyboard_1_data[2:0]}), .b({1'b0, and_2_out[3], 2'b00, and_2_out[3]}), .out(out_18));  // open: cin, cout
  Multiplexer #(.width(4), .enable("false")) multiplexer_1 (
    .in0(keyboard_1_data[3:0]), .in1(out_18[3:0]), .out(out_16), .sel(and_2_out[3]));
  Counter counter_1 (.Q(counter_1_q), .clk(clock), .clr(or_1_out));  // open: load, D, count, carry
  or or_1 (or_1_out, Reset_Phase_2, Reset);
  Counter #(.width(2), .max('h3)) counter_2 (
    .Q(counter_2_q), .clk(clock), .clr(or_2_out));  // open: load, D, count, carry
  or or_2 (or_2_out, or_3_out, and_6_out, and_3_p2);
  // AND_Gate and_3: pin names not known; wires that end beside it: Reset, and_3_p2, counter_2_q[0], counter_2_q[1]
  or or_3 (or_3_out, Reset_Phase_2, Reset);
  AddInstructions addinstructions_1 (
    .\input (ram_1_data), .add(two), .clock(clock), .\output (addinstructions_1_output), .reset(or_5_out));
  RAM #(.dataWidth(4), .bus("separate")) ram_1 (
    .addr(counter_1_q), .din(out_16), .data(ram_1_data), .str(Writing_Phase_1), .clk(clock),
    .ld(Writing_Phase_2), .clr(Reset));  // open: sel
  or or_4 (two, and_4_out, and_6_out);
  and and_4 (and_4_out, counter_2_q[0], not_2_out);
  not not_2 (not_2_out, counter_2_q[1]);
  or or_5 (or_5_out, Reset_Phase_2, Reset_Phase_2, Reset, Reset);
  Counter #(.width(3), .max('h7)) counter_3 (
    .Q(counter_3_q), .clk(clock), .clr(or_6_out));  // open: load, D, count, carry
  or or_6 (or_6_out, or_7_out, and_5_out);
  and and_5 (and_5_out, not_4_out, not_5_out, counter_3_q[2]);
  or or_7 (or_7_out, Reset_Phase_2, Reset_Phase_2, Reset, Reset);
  Counter counter_4 (.Q(counter_4_q), .clk(two), .clr(or_8_out));  // open: load, D, count, carry
  or or_8 (or_8_out, Reset_Phase_2, Reset_Phase_2, Reset, Reset);
  and and_6 (and_6_out, counter_3_q[0], counter_3_q[1], not_3_out);
  not not_3 (not_3_out, counter_3_q[2]);
  not not_4 (not_4_out, counter_3_q[0]);
  not not_5 (not_5_out, counter_3_q[1]);
  Multiplexer #(.width(8), .enable("false")) multiplexer_2 (
    .in0(address), .in1(counter_4_q), .out(multiplexer_2_out), .sel(Writing_Phase_2));
  Multiplexer #(.width(8), .enable("false")) multiplexer_3 (
    .in0(dbus), .in1(addinstructions_1_output), .out(multiplexer_3_out), .sel(Writing_Phase_2));
  or or_9 (or_9_out, Writing_Phase_2, Writing_Phase_2);
  RAM #(.bus("separate")) ram_2 (
    .addr(multiplexer_2_out), .din(multiplexer_3_out), .data(datain), .str(or_9_out), .clk(clock), .clr(Reset));  // open: sel, ld
  Clock clock_1 (.out(c));
  Multiplexer #(.select(2), .width(8), .enable("false")) multiplexer_4 (
    .in0(register_1_q), .in1(Immediate_q), .in2(sbus), .in3(dbus), .out(address), .sel(out_7));
  Register_part Immediate (.D(datain), .en(imload), .Q(Immediate_q), .clk(clock));  // open: clr
  Register_part Instruction_Register (.D(datain), .en(irload), .Q(Instruction_Register_q), .clk(clock));  // open: clr
  Decoder Decoder (
    .in_1(Instruction_Register_q), .zero(register_2_zero), .negative(register_2_negative), .phase(phase),
    .dregsel(dregsel), .sregsel(sregsel), .aluop(aluop), .pcload(pcload), .imload(imload), .pcsel(pcsel),
    .irload(irload), .readwrite(readwrite), .regsel(regsel), .dwrite(dwrite), .addrsel(out_7));
  Multiplexer #(.select(2), .width(8), .enable("false")) multiplexer_5 (
    .in0(Immediate_q), .in1(sbus), .in2(datain), .in3(aluout), .out(dval), .sel(regsel));
  Multiplexer #(.width(8), .enable("false")) multiplexer_6 (
    .in0(Immediate_q), .in1(pc_adder_1_pc_out), .out(multiplexer_6_out), .sel(pcsel));
  Register_part register_1 (.D(multiplexer_6_out), .en(pcload), .Q(register_1_q), .clk(clock), .clr(or_10_out));
  or or_10 (or_10_out, Reset, Reset_Phase_2);
  PC_Adder pc_adder_1 (.PC_in(register_1_q), .PC_out(pc_adder_1_pc_out));
  Register register_2 (
    .dwrite(dwrite), .dval(dval), .r3(r3), .r0(r0), .r1(r1), .r2(r2), .reset(or_10_out), .dregsel(dregsel),
    .sregsel(sregsel), .dbus(dbus), .zero(register_2_zero), .Negative(register_2_negative), .sbus(sbus));
  ALU ALU (.A(dbus), .B(sbus), .OP(aluop), .Result(aluout));

  // Other names for the same wires on the sheet: addrsel[1:0] = out_7; reset2 = Reset_Phase_2;
  //   writing = Writing_Phase_1; writing2 = Writing_Phase_2

  // Notes on the sheet:
  //   Register Output
endmodule

module ALU (
  input  [7:0] A,
  input  [7:0] B,
  input  [1:0] OP,
  output [7:0] Result
);

  wire [7:0] adder_1_out, and_1_out, or_1_out, subtractor_1_out, undriven;

  assign and_1_out = A & B & undriven;  // AND_Gate and_1, 8 bits wide
  assign or_1_out = undriven | A | B;  // OR_Gate or_1, 8 bits wide
  Adder adder_1 (.a(A), .b(B), .out(adder_1_out));  // open: cin, cout
  Subtractor subtractor_1 (.a(A), .b(B), .out(subtractor_1_out));  // open: bin, bout
  Multiplexer #(.select(2), .width(8), .enable("false")) multiplexer_1 (
    .in0(and_1_out), .in1(or_1_out), .in2(adder_1_out), .in3(subtractor_1_out), .out(Result), .sel(OP));
endmodule

module Decoder (
  input  [7:0] in_1,
  input  zero,
  input  negative,
  output [1:0] phase,
  output [1:0] dregsel,
  output [1:0] sregsel,
  output [1:0] aluop,
  output pcload,
  output imload,
  output pcsel,
  output irload,
  output readwrite,
  output [1:0] regsel,
  output dwrite,
  output [1:0] addrsel
);

  wire and_1_out, and_2_out, and_3_out, and_4_out, and_5_out, clock_1_out, multiplexer_7_out,
       multiplexer_9_out, not_1_out, not_2_out, not_3_out, not_4_out, or_1_out;
  wire [1:0] multiplexer_4_out, multiplexer_10_out;

  not not_1 (not_1_out, in_1[5]);
  and and_1 (and_1_out, in_1[4], not_1_out, in_1[6]);
  Multiplexer #(.select(2), .enable("false")) multiplexer_1 (
    .in0(1'b1), .in1(1'b0), .in2(1'b0), .in3(1'b0), .out(irload), .sel(phase));
  Multiplexer #(.select(2), .enable("false")) multiplexer_2 (
    .in0(1'b0), .in1(1'b0), .in2(and_1_out), .in3(1'b0), .out(readwrite), .sel(phase));
  Multiplexer #(.select(2), .enable("false")) multiplexer_3 (
    .in0(1'b0), .in1(in_1[7]), .in2(1'b0), .in3(1'b0), .out(imload), .sel(phase));
  Multiplexer #(.select(4), .width(2), .enable("false")) multiplexer_4 (
    .in0(2'b11), .in1(2'b11), .in2(2'b11), .in3(2'b11), .in4(2'b10), .in5(2'b00), .in6(2'b01), .in7(2'b00),
    .in8(2'b00), .in9(2'b00), .in10(2'b00), .in11(2'b00), .in12(2'b10), .in13(2'b00), .in14(2'b00),
    .in15(2'b00), .out(multiplexer_4_out), .sel(in_1[7:4]));
  Multiplexer #(.select(2), .width(2), .enable("false")) multiplexer_5 (
    .in0(2'b00), .in1(2'b00), .in2(multiplexer_4_out), .in3(2'b00), .out(regsel), .sel(phase));
  Clock clock_1 (.out(clock_1_out));
  Multiplexer #(.select(2), .enable("false")) multiplexer_6 (
    .in0(1'b1), .in1(1'b1), .in2(1'b0), .in3(1'b0), .out(pcsel), .sel(phase));
  Counter #(.width(2), .max('h3)) counter_1 (
    .Q(phase), .clk(clock_1_out), .clr(and_2_out));  // open: load, D, count, carry
  and and_2 (and_2_out, phase[1], phase[0]);
  Multiplexer #(.select(4), .enable("false")) multiplexer_7 (
    .in0(1'b1), .in1(1'b1), .in2(1'b1), .in3(1'b1), .in4(1'b1), .in5(1'b0), .in6(1'b1), .in7(1'b0),
    .in8(1'b0), .in9(1'b0), .in10(1'b0), .in11(1'b0), .in12(1'b1), .in13(1'b0), .in14(1'b1), .in15(1'b0),
    .out(multiplexer_7_out), .sel(in_1[7:4]));
  not not_2 (not_2_out, zero);
  not not_3 (not_3_out, negative);
  Multiplexer #(.select(2), .enable("false")) multiplexer_8 (
    .in0(1'b0), .in1(1'b0), .in2(multiplexer_7_out), .in3(1'b0), .out(dwrite), .sel(phase));
  and and_3 (and_3_out, not_2_out, not_3_out);
  not not_4 (not_4_out, in_1[6]);
  Multiplexer #(.select(2), .enable("false")) multiplexer_9 (
    .in0(zero), .in1(not_2_out), .in2(and_3_out), .in3(negative), .out(multiplexer_9_out), .sel(in_1[5:4]));
  and and_4 (and_4_out, not_4_out, in_1[7], multiplexer_9_out);
  and and_5 (and_5_out, in_1[4], in_1[5], in_1[6], in_1[7]);
  Multiplexer #(.select(4), .width(2), .enable("false")) multiplexer_10 (
    .in0(2'b00), .in1(2'b00), .in2(2'b00), .in3(2'b00), .in4(2'b10), .in5(2'b10), .in6(2'b00), .in7(2'b00),
    .in8(2'b00), .in9(2'b00), .in10(2'b00), .in11(2'b00), .in12(2'b00), .in13(2'b01), .in14(2'b01),
    .in15(2'b00), .out(multiplexer_10_out), .sel(in_1[7:4]));
  or or_1 (or_1_out, and_4_out, and_5_out);
  Multiplexer #(.select(2), .width(2), .enable("false")) multiplexer_11 (
    .in0(2'b00), .in1(2'b00), .in2(multiplexer_10_out), .in3(2'b00), .out(addrsel), .sel(phase));
  Multiplexer #(.select(2), .enable("false")) multiplexer_12 (
    .in0(1'b1), .in1(in_1[7]), .in2(or_1_out), .in3(1'b0), .out(pcload), .sel(phase));

  assign aluop = in_1[5:4];
  assign dregsel = in_1[3:2];
  assign sregsel = in_1[1:0];

  // Other names for the same wires on the sheet: irbit4 = in_1[4]; op1op2[3:0] = in_1[7:4]; op2[1:0] = in_1[5:4];
  //   irbit5 = in_1[5]; irbit6 = in_1[6]; op1[1:0] = in_1[7:6]; irbit7 = in_1[7]; Rd[1:0] = in_1[3:2];
  //   Rs[1:0] = in_1[1:0]

  // Notes on the sheet:
  //   Read/Write
  //   IR Load
  //   Register Select
  //   Immediate Load
  //   PC Select
  //   Phase Counter
  //   Destination Register Write
  //   Address Select
  //   PC Load
endmodule

module Register (
  input  dwrite,
  input  [1:0] dregsel,
  input  [7:0] dval,
  input  [1:0] sregsel,
  input  reset,
  output [7:0] r0,
  output [7:0] dbus,
  output [7:0] r1,
  output zero,
  output [7:0] r2,
  output Negative,
  output [7:0] r3,
  output [7:0] sbus
);

  wire clock_1_out, demultiplexer_1_out0, demultiplexer_1_out1, demultiplexer_1_out2, demultiplexer_1_out3,
       or_1_out;

  Demultiplexer #(.select(2), .enable("false")) demultiplexer_1 (
    .out0(demultiplexer_1_out0), .out1(demultiplexer_1_out1), .out2(demultiplexer_1_out2),
    .out3(demultiplexer_1_out3), .in(dwrite), .sel(dregsel));
  Clock clock_1 (.out(clock_1_out));
  Register_part register_1 (.D(dval), .en(demultiplexer_1_out0), .Q(r0), .clk(clock_1_out), .clr(reset));
  Register_part register_2 (.D(dval), .en(demultiplexer_1_out1), .Q(r1), .clk(clock_1_out), .clr(reset));
  Register_part register_3 (.D(dval), .en(demultiplexer_1_out2), .Q(r2), .clk(clock_1_out), .clr(reset));
  Register_part register_4 (.D(dval), .en(demultiplexer_1_out3), .Q(r3), .clk(clock_1_out), .clr(reset));
  Multiplexer #(.select(2), .width(8), .enable("false")) multiplexer_1 (
    .in0(r0), .in1(r1), .in2(r2), .in3(r3), .out(dbus), .sel(dregsel));
  Multiplexer #(.select(2), .width(8), .enable("false")) multiplexer_2 (
    .in0(r0), .in1(r1), .in2(r2), .in3(r3), .out(sbus), .sel(sregsel));
  or or_1 (or_1_out, dbus[0], dbus[1], dbus[2], dbus[3], dbus[4], dbus[5], dbus[6], dbus[7]);
  not not_1 (zero, or_1_out);

  assign Negative = dbus[7];

  // Other names for the same wires on the sheet: drs[1:0] = dregsel
endmodule

module PC_Adder (
  input  [7:0] PC_in,
  output [7:0] PC_out
);

  Adder adder_1 (.a(PC_in), .b(8'h1), .out(PC_out), .cin(1'b0));  // open: cout
endmodule

module Keyboard (
  input  clock,
  input  Writing_Phase_1,
  input  Writing_Phase_2,
  input  Reset_Phase_2,
  input  Reset,
  output [7:0] \output ,
  output [3:0] out_7,
  output [4:0] out_8
);

  wire and_3_p2, and_4_out, and_5_out, and_6_out, clock_t, not_1_out, not_2_out, not_3_out, not_4_out,
       not_5_out, or_1_out, or_2_out, or_3_out, or_4_out, or_6_out, or_7_out, or_8_out, two;
  wire [1:0] counter_2_q;
  wire [2:0] counter_3_q;
  wire [3:0] ram_1_data;
  wire [3:3] and_2_out;
  wire [6:0] keyboard_1_data;
  wire [7:0] addinstructions_1_output, counter_1_q, counter_4_q;

  Keyboard_part keyboard_1 (.clk(clock_t), .re(Writing_Phase_1), .clr(Reset), .data(keyboard_1_data));  // open: avail
  not not_1 (not_1_out, Reset);
  and and_1 (clock_t, not_1_out, clock);
  and and_2 (and_2_out[3], keyboard_1_data[5], keyboard_1_data[6], 1'b1);
  Adder #(.width(5)) adder_1 (
    .a({2'b00, keyboard_1_data[2:0]}), .b({1'b0, and_2_out[3], 2'b00, and_2_out[3]}), .out(out_8));  // open: cin, cout
  Multiplexer #(.width(4), .enable("false")) multiplexer_1 (
    .in0(keyboard_1_data[3:0]), .in1(out_8[3:0]), .out(out_7), .sel(and_2_out[3]));
  or or_1 (or_1_out, Reset_Phase_2, Reset);
  Counter counter_1 (.Q(counter_1_q), .clk(clock_t), .clr(or_2_out));  // open: load, D, count, carry
  or or_2 (or_2_out, Reset_Phase_2, Reset);
  Counter #(.width(2), .max('h3)) counter_2 (
    .Q(counter_2_q), .clk(clock_t), .clr(or_3_out));  // open: load, D, count, carry
  or or_3 (or_3_out, or_1_out, and_6_out, and_3_p2);
  // AND_Gate and_3: pin names not known; wires that end beside it: Reset, and_3_p2, counter_2_q[0], counter_2_q[1]
  RAM #(.dataWidth(4), .bus("separate")) ram_1 (
    .addr(counter_1_q), .din(out_7), .data(ram_1_data), .str(Writing_Phase_1), .clk(clock_t),
    .ld(Writing_Phase_2), .clr(Reset));  // open: sel
  and and_4 (and_4_out, counter_2_q[0], not_2_out);
  not not_2 (not_2_out, counter_2_q[1]);
  AddInstructions addinstructions_1 (
    .\input (ram_1_data), .add(two), .clock(clock_t), .\output (addinstructions_1_output), .reset(or_4_out));
  or or_4 (or_4_out, Reset_Phase_2, Reset_Phase_2, Reset, Reset);
  or or_5 (two, and_4_out, and_6_out);
  Counter #(.width(3), .max('h7)) counter_3 (
    .Q(counter_3_q), .clk(clock_t), .clr(or_6_out));  // open: load, D, count, carry
  or or_6 (or_6_out, or_7_out, and_5_out);
  and and_5 (and_5_out, not_3_out, not_4_out, counter_3_q[2]);
  or or_7 (or_7_out, Reset_Phase_2, Reset_Phase_2, Reset, Reset);
  Counter counter_4 (.Q(counter_4_q), .clk(two), .clr(or_8_out));  // open: load, D, count, carry
  or or_8 (or_8_out, Reset_Phase_2, Reset_Phase_2, Reset, Reset);
  and and_6 (and_6_out, counter_3_q[0], counter_3_q[1], not_5_out);
  not not_3 (not_3_out, counter_3_q[0]);
  not not_4 (not_4_out, counter_3_q[1]);
  not not_5 (not_5_out, counter_3_q[2]);
  RAM #(.bus("separate")) ram_2 (
    .addr(counter_4_q), .din(addinstructions_1_output), .data(\output ), .str(Writing_Phase_2),
    .clk(clock_t), .ld(clock_t), .clr(Reset));  // open: sel

  // Other names for the same wires on the sheet: reset2 = Reset_Phase_2; writing = Writing_Phase_1;
  //   writing2 = Writing_Phase_2
endmodule

module AddInstructions (
  input  [3:0] \input ,
  input  reset,
  input  add,
  input  clock,
  output [7:0] \output 
);

  wire [7:0] adder_1_out, multiplexer_1_out, shifter_1_out;

  Shifter shifter_1 (.in(\output ), .\dist (3'b100), .out(shifter_1_out));
  Adder adder_1 (.a({4'b0000, \input }), .b(shifter_1_out), .out(adder_1_out));  // open: cin, cout
  Multiplexer #(.width(8), .enable("false")) multiplexer_1 (
    .in0({4'b0000, \input }), .in1(adder_1_out), .out(multiplexer_1_out), .sel(add));
  Register_part register_1 (.D(multiplexer_1_out), .Q(\output ), .clk(clock), .clr(reset));  // open: en
endmodule
